# Fritzing sketch XIAO SOCD Cleaner (direct) (saved by Fritzing 0.9.5d)
breadboards: 1

parts:
  Mod1 = seeeduino-xiao
  Output = female alternating pin header, 5 pins [form="♀ (female)"]
  Input = female alternating pin header, 5 pins [form="♀ (female)"]
  POWER = female pin header, 2 pins [form="♀ (female)"]
  SW1 = DIP SWITCH [package=dipswitch-02]

nets:
  N1: Mod1.D0, Input.pin4
  N2: Mod1.D1, Input.pin3
  N3: Mod1.D2, Input.pin2
  N4: Mod1.D3, Input.pin1
  N5: Mod1.D4, Output.pin4
  N6: Mod1.D5, SW1.3
  N7: Mod1.D6, SW1.4
  N8: Mod1.D8, Output.pin3
  N9: Mod1.D9, Output.pin2
  N10: Mod1.D10, Output.pin1
  N11: Mod1.3V3, POWER.pin2
  N12: Mod1.GND, Output.pin5, Input.pin5, POWER.pin1, SW1.1, SW1.2

custom parts:
  seeeduino-xiao: Seeeduino XIAO processor board.
