# Fritzing sketch XIAO SOCD Cleaner (saved by Fritzing 0.9.5d)
breadboards: 1

parts:
  Mod1 = seeeduino-xiao
  R1 = Resistor [tolerance=±5% resistance=100 package=THT]
  PC847 = IC, DIP package, 16 pins [chip_label=PC847]
  R2 = Resistor [tolerance=±5% resistance=100 package=THT]
  R3 = Resistor [tolerance=±5% resistance=100 package=THT]
  R4 = Resistor [tolerance=±5% resistance=100 package=THT]
  Output = female alternating pin header, 5 pins [form="♀ (female)"]
  Input = female alternating pin header, 5 pins [form="♀ (female)"]
  POWER = female pin header, 2 pins [form="♀ (female)"]
  SW1 = DIP SWITCH [package=dipswitch-02]

nets:
  N1: Mod1.D0, Input.pin4
  N2: Mod1.D1, Input.pin3
  N3: Mod1.D2, Input.pin2
  N4: Mod1.D3, Input.pin1
  N5: Mod1.D4, R1.Pin_1
  N6: Mod1.D5, SW1.3
  N7: Mod1.D6, SW1.4
  N8: Mod1.D8, R4.Pin_1
  N9: Mod1.D9, R3.Pin_1
  N10: Mod1.D10, R2.Pin_1
  N11: Mod1.3V3, POWER.pin2
  N12: Mod1.GND, Input.pin5, SW1.1, SW1.2
  N13: R1.Pin_0, PC847.pin7
  N14: PC847.pin1, R2.Pin_0
  N15: PC847.pin2, PC847.pin4, PC847.pin6, PC847.pin8, POWER.pin1
  N16: PC847.pin3, R3.Pin_0
  N17: PC847.pin5, R4.Pin_0
  N18: PC847.pin9, PC847.pin11, PC847.pin13, PC847.pin15, Output.pin5
  N19: PC847.pin10, Output.pin4
  N20: PC847.pin12, Output.pin3
  N21: PC847.pin14, Output.pin2
  N22: PC847.pin16, Output.pin1

custom parts:
  seeeduino-xiao: Seeeduino XIAO processor board.
